# Fritzing sketch antikolasjons system (saved by Fritzing 0.9.10b)
breadboards: 1

parts:
  HC-SR04_Sensor_1 = HC-SR04 Ultrasonic Distance Sensor
  Part1 = Arduino Uno (Rev3) - ICSP
  Mod1 = KY-016 RGB Full Color LED Module [package="Breakout board"]
  buz1 = Piezo Buzzer

nets:
  VCC: HC-SR04_Sensor_1.VCC, Part1.5V
  N1: HC-SR04_Sensor_1.TRIG, Part1.D9_PWM
  N2: HC-SR04_Sensor_1.ECHO, Part1.D10_PWM/SS
  GND: HC-SR04_Sensor_1.GND, Part1.GND, Mod1.-, buz1.pin_2
  N3: Part1.D8, buz1.pin_1
  N4: Part1.D3_PWM, Mod1.R
  N5: Part1.D5_PWM, Mod1.G
  N6: Part1.D6_PWM, Mod1.B

custom parts:
  KY-016 RGB Full Color LED Module: KY-016 Arduino full color 5mm RGB LED, different colors can be obtained by mixing the three primary colors.
  Piezo Buzzer: Part from https://www.nutsvolts.com/magazine/article/november2012_SmileysWorkshop. Breadboard and icon images modified to be 0.3" in spacing and be more similar to the actual physical part.
