# Fritzing sketch hand controller v1 (saved by Fritzing 0.9.10b)
stripboards: 1

parts:
  J1 = single row smd female pin header, 8 pins [form="♀ (female)"]
  J2 = single row smd female pin header, 8 pins [form="♀ (female)"]
  J3 = female pin header, 17 pins [form="♀ (female)"]
  Part1 = Arduino Nano (Rev3.0)
  J5 = female pin header, 2 pins [form="♀ (female)"]
  J6 = female pin header, 2 pins [form="♀ (female)"]
  J7 = female pin header, 4 pins [form="♀ (female)"]
  J8 = female pin header, 2 pins [form="♀ (female)"]
  J9 = female pin header, 2 pins [form="♀ (female)"]
  J10 = female pin header, 2 pins [form="♀ (female)"]
  R1 = Rotary Potentiometer (Small) [maximum_resistance=10kΩ knob_status=50% power=0.5W package=THT]
  VCC1 = Battery block 9V
  S2 = Round Pushbutton
  S3 = Round Pushbutton
  J11 = Camdenboss CTB0158-4 [part_number=CTB0158-4 package=THT]
  S4 = Round Pushbutton
  S5 = Round Pushbutton
  Display1 = LCD screen 16x2 IIC [part_number=101290]
  J4 = female pin header, 17 pins [form="♀ (female)"]
  JP1 = Header 2 [package=r_sw_th]

nets:
  N1: J1.pin1, J2.pin5, Part1.D9, J11.pin1, J4.pin6
  N2: J1.pin2, J2.pin6, Part1.D8, J11.pin2, J4.pin7
  N3: J1.pin3, J2.pin7, Part1.D7, J11.pin3, J4.pin8
  GND: J1.pin4, J2.pin8, J3.pin16, Part1.GND, J5.pin1, J5.pin2, J7.pin1, J7.pin2, J7.pin3, J7.pin4, J10.pin1, R1.leg1, VCC1.-, S2.leg0, S3.leg0, J11.pin4, S4.leg0, S5.leg0, Display1.GND, J4.pin14
  N4: J1.pin5, Part1.D5, S5.leg1, J4.pin10
  N5: J1.pin6, Part1.D4, S4.leg1, J4.pin11
  N6: J1.pin7, Part1.D3, S3.leg1, J4.pin12
  N7: J1.pin8, Part1.D2, S2.leg1, J4.pin13
  N8: J2.pin1, J4.pin2
  N9: J2.pin2, Part1.D12/MISO, J4.pin3
  N10: J2.pin3, Part1.D11/MOSI, J4.pin4
  N11: J2.pin4, Part1.D10, J4.pin5
  N12: J3.pin3, Part1.D13/SCK
  N13: J3.pin4, Part1.3V3
  N14: J3.pin5, Part1.AREF
  N15: J3.pin6, Part1.A0, J8.pin1, J8.pin2, R1.wiper
  N16: J3.pin7, Part1.A1
  N17: J3.pin8, Part1.A2
  N18: J3.pin9, Part1.A3
  N19: J3.pin10, Part1.A4, J9.pin1, Display1.SDA
  N20: J3.pin11, Part1.A5, J9.pin2, Display1.SCL
  N21: J3.pin12, Part1.A6
  N22: J3.pin13, Part1.A7
  5V: J3.pin14, Part1.5V, J6.pin1, J6.pin2, R1.leg2, Display1.VCC
  N23: J3.pin15, Part1.RESET, J4.pin15
  N24: J3.pin17, Part1.VIN, J10.pin2, JP1.1
  N25: Part1.D1/TX, J4.pin17
  N26: Part1.D0/RX, J4.pin16
  N27: Part1.D6, J4.pin9
  N28: VCC1.+, JP1.2

custom parts:
  LCD screen 16x2 IIC: LCD screen with HD44780 controller enables showing text, symbols, value or anything else that comes from Croduino/Arduino. It is capable of showing 16 symbols in two lines and therefore can be used in many projects that need to send clearly visible and legible output information.. • Color of symbols: White • Backlight: Blue • Dimensions: 80 x 36 x 12 mm • Screen dimensions: 64.5 x 16 mm •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
