# Fritzing sketch hånd kontroller (saved by Fritzing 1.0.0rc)
stripboards: 1

parts:
  Part1 = Arduino Nano (Rev3.0)
  S2 = Momentary Switch [package=ksa_sealed_tac_switch]
  R1 = Rotary Potentiometer (Small) [maximum_resistance=100kΩ knob_status=50% power=0.5W package=THT]
  Part2 = Adafruit I2C+SPI LCD Backpack [part_number="Adafruit #292"]
  U1 = LCD-16X2 [package=lcd-16x2]  # not connected
  S3 = Momentary Switch [package=ksa_sealed_tac_switch]
  S4 = Momentary Switch [package=ksa_sealed_tac_switch]
  S5 = Momentary Switch [package=ksa_sealed_tac_switch]
  J1 = female pin header, 4 pins [form="♀ (female)"]
  J2 = female pin header, 2 pins [form="♀ (female)"]
  J3 = female pin header, 1 pin [form="♀ (female)"]
  J4 = female pin header, 4 pins [form="♀ (female)"]
  J5 = female pin header, 2 pins [form="♀ (female)"]
  J6 = female pin header, 2 pins [form="♀ (female)"]
  VCC1 = Battery block 9V
  J7 = female pin header, 2 pins [form="♀ (female)"]
  J8 = female pin header, 4 pins [form="♀ (female)"]

nets:
  GND: Part1.GND, S2.3, R1.leg1, Part2.GND, S3.3, S4.3, S5.3, J1.pin1, J1.pin2, J1.pin3, J1.pin4, J6.pin1, J6.pin2, VCC1.-, J7.pin1
  N1: Part1.D2, S2.2, J4.pin4
  N2: Part1.D3, S3.2, J4.pin3
  N3: Part1.D4, S4.2, J4.pin2
  N4: Part1.D5, S5.2, J4.pin1
  N5: Part1.D8, J8.pin4
  N6: Part1.D9, J8.pin3
  N7: Part1.D10, J8.pin2
  N8: Part1.D11/MOSI, J8.pin1
  N9: Part1.VIN, VCC1.+, J7.pin2
  5V: Part1.5V, R1.leg2, Part2.VCC, J5.pin1, J5.pin2
  N10: Part1.A5, Part2.CLOCK, J2.pin2
  N11: Part1.A4, Part2.DATA, J2.pin1
  N12: Part1.A0, R1.wiper, J3.pin1

custom parts:
  Adafruit I2C+SPI LCD Backpack: LCD backpacks reduce the number of pins needed to connect to an LCD. LCDs are a fun and easy way to have your microcontroller project talk back to you. Character LCDs are common, and easy to get, available in tons of colors and sizes. We've written tutorials on using character LCDs with an Arduino (or similar microcontroller) but find that the number of pins necessary to control the LCD can be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
