# Fritzing sketch rgb led + dht11 (saved by Fritzing 0.9.10b)
breadboards: 1

parts:
  Part1 = Arduino Uno (Rev3) - ICSP
  LED1 = RGB LED (com. cathode, rgb) [package="5 mm [THT]"]
  R1 = Resistor [tolerance=±5% resistance=220 package="1206 [SMD]"]
  R2 = Resistor [tolerance=±5% resistance=220 package="1206 [SMD]"]
  R3 = Resistor [tolerance=±5% resistance=220 package="1206 [SMD]"]
  DHT1 = DHT11 Humitidy and Temperature Sensor (3 pins)

nets:
  5V: Part1.5V, DHT1.VDD
  GND: Part1.GND, LED1.common_cathode, DHT1.GND
  N1: Part1.D2, DHT1.DATA
  N2: Part1.D3_PWM, R1.Pin_0
  N3: Part1.D5_PWM, R3.Pin_0
  N4: Part1.D6_PWM, R2.Pin_0
  N5: LED1.red_anode, R1.Pin_1
  N6: LED1.green_anode, R2.Pin_1
  N7: LED1.blue_anode, R3.Pin_1

custom parts:
  DHT11 Humitidy and Temperature Sensor (3 pins): DHT11 Humidity and Temperature Sensor (3 pins) from the design created by John De Cristofaro for Adafruit Industries.
