# Fritzing sketch Trafikklys med vektcelle (saved by Fritzing 1.0.0rc)
stripboards: 1

parts:
  Part1 = Arduino Nano (Rev3.0)
  Load_Cell1 = Load Cell - Red/white/black/green
  J9 = female pin header, 2 pins [form="♀ (female)"]
  J13 = female pin header, 2 pins [form="♀ (female)"]
  J14 = female pin header, 2 pins [form="♀ (female)"]
  J16 = female pin header, 2 pins [form="♀ (female)"]
  J17 = female pin header, 2 pins [form="♀ (female)"]
  Part2 = HX711 Weighing Sensor Module
  J18 = male pin header, 6 pins [form="♂ (male)"]
  J10 = male pin header, 4 pins [form="♂ (male)"]
  J11 = male pin header, 6 pins [form="♂ (male)"]
  J19 = male pin header, 4 pins [form="♂ (male)"]

nets:
  GND: Part1.GND, J9.pin1, J9.pin2, J14.pin1, J17.pin1, J17.pin2, Part2.GND, J10.pin4, J19.pin4
  N1: Part1.D5, J13.pin2, Part2.CK/TX, J10.pin2, J19.pin2
  N2: Part1.D6, J13.pin1, Part2.DO/RX, J10.pin3, J19.pin3
  N3: Part1.D7, J14.pin2
  5V: Part1.5V, J16.pin1, J16.pin2, Part2.VCC, J10.pin1, J19.pin1
  N4: Load_Cell1.wire1, Part2.E+, J18.pin1, J11.pin1
  N5: Load_Cell1.wire2, Part2.A-, J18.pin4, J11.pin4
  N6: Load_Cell1.wire3, Part2.E-, J18.pin2, J11.pin2
  N7: Load_Cell1.wire4, Part2.A+, J18.pin3, J11.pin3
  N8: Part2.B+, J18.pin5, J11.pin5
  N9: Part2.B-, J18.pin6, J11.pin6

custom parts:
  Load Cell - Red/white/black/green: A rectangle load cell/weighting pressure Sensor with four wires - Red, white, black, green. Normally corresponding with E+, E-, A+, A- respectively.
