# Fritzing sketch teste å lage pcb ikke bugged (saved by Fritzing 1.0.0rc)
circuit board: 5cm x 5cm

parts:
  Part1 = Arduino Nano (Rev3.0)
  R1 = Resistor [tolerance=±5% power=0.25W resistance=220 package=THT]
  R2 = Resistor [tolerance=±5% power=0.25W resistance=1000 package=THT]
  S1 = Pushbutton [package="[THT]"]
  LED1 = LED - 5mm [color="Red (633nm)" current=0.030A package="5 mm [THT]"]

nets:
  N1: Part1.GND, R2.Pin_1, LED1.cathode
  N2: Part1.D2, R1.Pin_0
  N3: Part1.D8, R2.Pin_0, S1.Pin_3, S1.Pin_4
  N4: Part1.5V, S1.Pin_1
  N5: R1.Pin_1, LED1.anode
