# Fritzing sketch teste å lage pcb (saved by Fritzing 1.0.0rc)
circuit board: 8.46667cm x 5.64444cm

parts:
  Part1 = Arduino Nano (Rev3.0)
  LED1 = smd LED [color="Red (633nm)" package="0603 [SMD]"]
  S1 = Pushbutton [package="[THT]"]
  R2 = Resistor [tolerance=±5% power=0.25W resistance=220 package=THT]
  R3 = Resistor [tolerance=±5% power=0.25W resistance=1000 package=THT]

nets (from the schematic view):
  N1: Part1.GND, LED1.cathode, R3.Pin_1
  N2: Part1.D2, R2.Pin_0
  N3: Part1.D8, S1.Pin_3, S1.Pin_4, R3.Pin_0
  N4: Part1.5V, S1.Pin_1, S1.Pin_2
  N5: LED1.anode, R2.Pin_1
